// Logisim project Flip-Flops and Shift Registers.circ as structural Verilog: 1 circuit, main circuit main
module main (
  input  K,
  input  J,
  input  K_2,
  input  J_2,
  output Q,
  output Q_prime,
  output Q_2,
  output Q_prime_2
);

  wire and_1_out, and_2_out, clock_1_out;

  Clock clock_1 (.out(clock_1_out));
  and and_1 (and_1_out, Q, K, clock_1_out);
  and and_2 (and_2_out, clock_1_out, J, Q_prime);
  J_K_Flip_Flop j_k_ff_1 (.J(K_2), .clk(K_2), .K(J_2), .Q(Q_2), .Qn(Q_prime_2));  // open: preset, en, reset
  nor nor_1 (Q, and_1_out, Q_prime);
  nor nor_2 (Q_prime, Q, and_2_out);

  // Notes on the sheet:
  //   Clock
  //   Name: Akmam Hasan
  //   ID: 1911192642
  //   JK flip-flop using AND and NOR Gate
endmodule
