// Logisim project Synchronous Sequential Circuits.circ as structural Verilog: 1 circuit, main circuit main
module main (
  input  X,
  output Y
);

  wire and_1_out, j_k_ff_1_q, j_k_ff_1_qn, j_k_ff_2_q, j_k_ff_2_qn, not_1_out;

  not not_1 (not_1_out, X);
  J_K_Flip_Flop j_k_ff_1 (.J(X), .K(X), .Q(j_k_ff_1_q), .Qn(j_k_ff_1_qn));  // open: clk, preset, en, reset
  and and_1 (and_1_out, j_k_ff_1_qn, not_1_out);
  and and_2 (Y, j_k_ff_1_qn, X);
  J_K_Flip_Flop j_k_ff_2 (.J(and_1_out), .K(X), .Q(j_k_ff_2_q), .Qn(j_k_ff_2_qn));  // open: clk, preset, en, reset

  // Notes on the sheet:
  //   Name: Akmam Hasan
  //   ID: 1911192642
  //   A
  //   A'
  //   B
  //   B'
endmodule
